# Fritzing sketch PanTiltCam (saved by Fritzing 0.9.3b)
breadboards: 1

parts:
  Raspberry_Pi_1 = Raspberry Pi 3 [part_number=RPI-3-V1.2]
  J3 = Power Jack [package=power_jack_combo]  # not connected
  J2 = Basic Servo
  J1 = Basic Servo

nets:
  GND: Raspberry_Pi_1.GND, J2.gnd, J1.gnd
  N1: Raspberry_Pi_1.GPIO17, J2.pulse
  N2: Raspberry_Pi_1.GPIO27, J1.pulse
  VCC: J2.vcc, J1.vcc

notes:
  GPIO 17
  GPIO 27
  TILT Servo
  PAN
  Servo
  External 5VDC
  Servo Power supply
